# Fritzing sketch main (saved by Fritzing 0.9.10b)
breadboards: 1

parts:
  Bauteil1 = Arduino MKR1000
  LCD1 = LCD screen
  U1 = GAS_SENSOR [package=mq-3]
  R1 = Resistor [tolerance=±5% resistance=220 package="0805 [SMD]"]
  J1 = Piezo Speaker
  S2 = Pushbutton [package="[SMD]"]
  R2 = Resistor [tolerance=±5% resistance=10000 package="1206 [SMD]"]

nets:
  N1: Bauteil1.A1, U1.B1
  N2: Bauteil1.A3, LCD1.V0
  N3: Bauteil1.D0, S2.Pin_3, S2.Pin_4, R2.Pin_1
  N4: Bauteil1.D2_PWM, LCD1.DB4
  N5: Bauteil1.D3_PWM, LCD1.DB5
  N6: Bauteil1.D4_PWM, LCD1.DB6
  N7: Bauteil1.D5_PWM, LCD1.DB7
  N8: Bauteil1.D11_SDA, LCD1.E
  N9: Bauteil1.D12_SCL, LCD1.RS
  GND: Bauteil1.GND, LCD1.VSS, LCD1.R/W, LCD1.LED-, U1.H1, J1.pin1, S2.Pin_1, S2.Pin_2
  5V: Bauteil1.5V, LCD1.VDD, U1.H2, R1.Pin_0, R2.Pin_0
  N10: LCD1.LED+, R1.Pin_1

custom parts:
  Arduino MKR1000: MKR1000 is a powerful board that combines the functionality of the Zero and the Wi-Fi Shield. It is the ideal solution for makers wanting to design IoT projects with minimal previous experience in networking
