# Fritzing sketch second (saved by Fritzing 0.9.10b)
breadboards: 1

parts:
  Bauteil1 = Arduino MKR1000
  Bauteil2 = RFID-RC522-v2
  R3 = Resistor [tolerance=±5% resistance=1000 package="1206 [SMD]"]
  R4 = Resistor [tolerance=±5% resistance=1000 package="1206 [SMD]"]
  R5 = Resistor [tolerance=±5% resistance=1000 package="1206 [SMD]"]
  J1 = Piezo Speaker

nets (from the breadboard view):
  N1: Bauteil1.D0, J1.pin2
  N2: Bauteil1.D6, Bauteil2.RST
  N3: Bauteil1.D7, Bauteil2.SDA
  N4: Bauteil1.D8_MOSI, Bauteil2.MOSI
  N5: Bauteil1.D9_SCK, Bauteil2.SCK
  N6: Bauteil1.D10_MISO, Bauteil2.MISO
  GND: Bauteil1.GND, Bauteil2.GND, R5.Pin_1, J1.pin1
  5V: Bauteil1.5V, Bauteil2.3.3V, R3.Pin_1, R4.Pin_0, R4.Pin_1
  N7: R3.Pin_0, R5.Pin_0

custom parts:
  Arduino MKR1000: MKR1000 is a powerful board that combines the functionality of the Zero and the Wi-Fi Shield. It is the ideal solution for makers wanting to design IoT projects with minimal previous experience in networking
  RFID-RC522-v2: A simple China made RFID-RC522 Reader; do check the pin labels, as this is a MFRC522 based clone.
